# Fritzing sketch 64 analog input (saved by Fritzing 0.7.11b)

parts:
  MUX5 = 74TH/HCT4051 [chip_label="74TH 4051" package="DIP (Dual Inline) [THT]"]
  MUX7 = 74TH/HCT4051 [chip_label="74TH 4051" package="DIP (Dual Inline) [THT]"]
  MUX6 = 74TH/HCT4051 [chip_label="74TH 4051" package="DIP (Dual Inline) [THT]"]
  MUX4 = 74TH/HCT4051 [chip_label="74TH 4051" package="DIP (Dual Inline) [THT]"]
  J2 = female pin header, 8 pins [form="♀ (female)"]
  J3 = female pin header, 8 pins [form="♀ (female)"]
  J4 = female pin header, 8 pins [form="♀ (female)"]
  J5 = female pin header, 4 pins [form="♀ (female)"]
  J1 = female pin header, 4 pins [form="♀ (female)"]
  J6 = female pin header, 4 pins [form="♀ (female)"]
  J7 = female pin header, 8 pins [form="♀ (female)"]
  J8 = female pin header, 8 pins [form="♀ (female)"]
  J9 = female pin header, 8 pins [form="♀ (female)"]
  J10 = female pin header, 4 pins [form="♀ (female)"]
  MUX3 = 74TH/HCT4051 [chip_label="74TH 4051" package="DIP (Dual Inline) [THT]"]
  MUX0 = 74TH/HCT4051 [chip_label="74TH 4051" package="DIP (Dual Inline) [THT]"]
  MUX1 = 74TH/HCT4051 [chip_label="74TH 4051" package="DIP (Dual Inline) [THT]"]
  MUX2 = 74TH/HCT4051 [chip_label="74TH 4051" package="DIP (Dual Inline) [THT]"]
  5V = female pin header, 1 pin [form="♀ (female)"]
  GND = female pin header, 1 pin [form="♀ (female)"]
  4051 = 74TH/HCT4051 [chip_label="74TH 4051" package="DIP (Dual Inline) [THT]"]
  s0s1s2 = female pin header, 3 pins [form="♀ (female)"]
  J11 = female pin header, 4 pins [form="♀ (female)"]
  J12 = female pin header, 4 pins [form="♀ (female)"]
  J13 = female pin header, 4 pins [form="♀ (female)"]
  J14 = female pin header, 4 pins [form="♀ (female)"]
  J15 = female pin header, 8 pins [form="♀ (female)"]
  J16 = female pin header, 8 pins [form="♀ (female)"]
  J17 = female pin header, 8 pins [form="♀ (female)"]
  J18 = female pin header, 8 pins [form="♀ (female)"]
  J19 = female pin header, 8 pins [form="♀ (female)"]
  J20 = female pin header, 8 pins [form="♀ (female)"]
  J21 = female pin header, 8 pins [form="♀ (female)"]
  J22 = female pin header, 8 pins [form="♀ (female)"]
  J23 = female pin header, 8 pins [form="♀ (female)"]
  J24 = female pin header, 8 pins [form="♀ (female)"]
  J25 = female pin header, 8 pins [form="♀ (female)"]
  J26 = female pin header, 8 pins [form="♀ (female)"]
  J27 = female pin header, 4 pins [form="♀ (female)"]
  J28 = female pin header, 4 pins [form="♀ (female)"]
  J29 = female pin header, 4 pins [form="♀ (female)"]
  J30 = female pin header, 4 pins [form="♀ (female)"]
  OUT = female pin header, 1 pin [form="♀ (female)"]
  s3s4s5 = female pin header, 3 pins [form="♀ (female)"]

nets:
  N1: MUX5.Y4, J1.pin2
  N2: MUX5.Y6, J1.pin1
  N3: MUX5.Z, 4051.Y5
  N4: MUX5.Y7, J1.pin3
  N5: MUX5.Y5, J1.pin4
  GND: MUX5.E, MUX5.GND, MUX7.E, MUX7.GND, MUX6.E, MUX6.GND, MUX4.E, MUX4.GND, MUX3.E, MUX3.GND, MUX0.E, MUX0.GND, MUX1.E, MUX1.GND, MUX2.E, MUX2.GND, GND.pin1, 4051.E, 4051.GND, J11.pin1, J11.pin2, J11.pin3, J11.pin4, J13.pin1, J13.pin2, J13.pin3, J13.pin4, J15.pin1, J15.pin2, J15.pin3, J15.pin4, J15.pin5, J15.pin6, J15.pin7, J15.pin8, J17.pin1, J17.pin2, J17.pin3, J17.pin4, J17.pin5, J17.pin6, J17.pin7, J17.pin8, J19.pin1, J19.pin2, J19.pin3, J19.pin4, J19.pin5, J19.pin6, J19.pin7, J19.pin8, J21.pin1, J21.pin2, J21.pin3, J21.pin4, J21.pin5, J21.pin6, J21.pin7, J21.pin8, J23.pin1, J23.pin2, J23.pin3, J23.pin4, J23.pin5, J23.pin6, J23.pin7, J23.pin8, J25.pin1, J25.pin2, J25.pin3, J25.pin4, J25.pin5, J25.pin6, J25.pin7, J25.pin8, J27.pin1, J27.pin2, J27.pin3, J27.pin4, J29.pin1, J29.pin2, J29.pin3, J29.pin4
  N6: MUX5.S2, MUX7.S2, MUX6.S2, MUX4.S2, MUX3.S2, MUX0.S2, MUX1.S2, MUX2.S2, s3s4s5.pin1
  N7: MUX5.S1, MUX7.S1, MUX6.S1, MUX4.S1, MUX3.S1, MUX0.S1, MUX1.S1, MUX2.S1, s3s4s5.pin2
  N8: MUX5.S0, MUX7.S0, MUX6.S0, MUX4.S0, MUX3.S0, MUX0.S0, MUX1.S0, MUX2.S0, s3s4s5.pin3
  N9: MUX5.Y3, J2.pin5
  N10: MUX5.Y0, J2.pin6
  N11: MUX5.Y1, J2.pin7
  N12: MUX5.Y2, J2.pin8
  VCC: MUX5.Vcc, MUX7.Vcc, MUX6.Vcc, MUX4.Vcc, MUX3.Vcc, MUX0.Vcc, MUX1.Vcc, MUX2.Vcc, 5V.pin1, 4051.Vcc, J12.pin1, J12.pin2, J12.pin3, J12.pin4, J14.pin1, J14.pin2, J14.pin3, J14.pin4, J16.pin1, J16.pin2, J16.pin3, J16.pin4, J16.pin5, J16.pin6, J16.pin7, J16.pin8, J18.pin1, J18.pin2, J18.pin3, J18.pin4, J18.pin5, J18.pin6, J18.pin7, J18.pin8, J20.pin1, J20.pin2, J20.pin3, J20.pin4, J20.pin5, J20.pin6, J20.pin7, J20.pin8, J22.pin1, J22.pin2, J22.pin3, J22.pin4, J22.pin5, J22.pin6, J22.pin7, J22.pin8, J24.pin1, J24.pin2, J24.pin3, J24.pin4, J24.pin5, J24.pin6, J24.pin7, J24.pin8, J26.pin1, J26.pin2, J26.pin3, J26.pin4, J26.pin5, J26.pin6, J26.pin7, J26.pin8, J28.pin1, J28.pin2, J28.pin3, J28.pin4, J30.pin1, J30.pin2, J30.pin3, J30.pin4
  N13: MUX7.Y4, J2.pin1
  N14: MUX7.Y6, J2.pin2
  N15: MUX7.Z, 4051.Y7
  N16: MUX7.Y7, J2.pin3
  N17: MUX7.Y5, J2.pin4
  N18: MUX7.Y3, J3.pin5
  N19: MUX7.Y0, J3.pin6
  N20: MUX7.Y1, J3.pin7
  N21: MUX7.Y2, J3.pin8
  N22: MUX6.Y4, J3.pin1
  N23: MUX6.Y6, J3.pin2
  N24: MUX6.Z, 4051.Y6
  N25: MUX6.Y7, J3.pin3
  N26: MUX6.Y5, J3.pin4
  N27: MUX6.Y3, J4.pin5
  N28: MUX6.Y0, J4.pin6
  N29: MUX6.Y1, J4.pin7
  N30: MUX6.Y2, J4.pin8
  N31: MUX4.Y4, J4.pin1
  N32: MUX4.Y6, J4.pin2
  N33: MUX4.Z, 4051.Y4
  N34: MUX4.Y7, J4.pin3
  N35: MUX4.Y5, J4.pin4
  N36: MUX4.Y3, J5.pin1
  N37: MUX4.Y0, J5.pin2
  N38: MUX4.Y1, J5.pin3
  N39: MUX4.Y2, J5.pin4
  N40: J6.pin1, MUX3.Y1
  N41: J6.pin2, MUX3.Y2
  N42: J6.pin3, MUX3.Y0
  N43: J6.pin4, MUX3.Y3
  N44: J7.pin1, MUX0.Y2
  N45: J7.pin2, MUX0.Y1
  N46: J7.pin3, MUX0.Y0
  N47: J7.pin4, MUX0.Y3
  N48: J7.pin5, MUX3.Y5
  N49: J7.pin6, MUX3.Y7
  N50: J7.pin7, MUX3.Y6
  N51: J7.pin8, MUX3.Y4
  N52: J8.pin1, MUX1.Y2
  N53: J8.pin2, MUX1.Y1
  N54: J8.pin3, MUX1.Y0
  N55: J8.pin4, MUX1.Y3
  N56: J8.pin5, MUX0.Y5
  N57: J8.pin6, MUX0.Y7
  N58: J8.pin7, MUX0.Y6
  N59: J8.pin8, MUX0.Y4
  N60: J9.pin1, MUX2.Y2
  N61: J9.pin2, MUX2.Y1
  N62: J9.pin3, MUX2.Y0
  N63: J9.pin4, MUX2.Y3
  N64: J9.pin5, MUX1.Y5
  N65: J9.pin6, MUX1.Y7
  N66: J9.pin7, MUX1.Y6
  N67: J9.pin8, MUX1.Y4
  N68: J10.pin1, MUX2.Y5
  N69: J10.pin2, MUX2.Y7
  N70: J10.pin3, MUX2.Y6
  N71: J10.pin4, MUX2.Y4
  N72: MUX3.Z, 4051.Y3
  N73: MUX0.Z, 4051.Y0
  N74: MUX1.Z, 4051.Y1
  N75: MUX2.Z, 4051.Y2
  N76: 4051.Z, OUT.pin1
  N77: 4051.S2, s0s1s2.pin1
  N78: 4051.S1, s0s1s2.pin2
  N79: 4051.S0, s0s1s2.pin3

notes:
  5V
  GND
  00
  01
  02
  03
  04
  06
  07
  05
  10
  14
  11
  13
  12
  08
  09
  18
  22
  19
  23
  20
  16
  17
  21
  25
  30
  27
  31
  28
  24
  26
  29
  34
  38
  36
  39
  32
  33
  37
  46
  45
  47
  42
  44
  43
  41
  40
  54
  53
  55
  50
  52
  51
  49
  48
  62
  61
  63
  58
  60
  59
  57
  56

custom parts:
  74TH/HCT4051: 8-channel analog multiplexer/demultiplexer
