# Fritzing sketch INPUT_PLATINE (saved by Fritzing 0.7.12b)

parts:
  74TH/HCT1 = 74TH/HCT4051 [chip_label="74TH 4051" package="DIP (Dual Inline) [THT]"]
  74TH/HCT2 = 74TH/HCT4051 [chip_label="74TH 4051" package="DIP (Dual Inline) [THT]"]
  74TH/HCT3 = 74TH/HCT4051 [chip_label="74TH 4051" package="DIP (Dual Inline) [THT]"]
  MCP23017_1 = MCP23017 [chip_label="MCP23017\n" package="DIP (Dual Inline) [THT]"]
  MCP23017_2 = MCP23017 [chip_label="MCP23017\n" package="DIP (Dual Inline) [THT]"]
  MCP23017_3 = MCP23017 [chip_label="MCP23017\n" package="DIP (Dual Inline) [THT]"]
  MCP23017_4 = MCP23017 [chip_label="MCP23017\n" package="DIP (Dual Inline) [THT]"]
  J3 = female pin header, 8 pins [form="♀ (female)"]
  J4 = female pin header, 8 pins [form="♀ (female)"]
  J5 = female pin header, 8 pins [form="♀ (female)"]
  J6 = female pin header, 8 pins [form="♀ (female)"]
  J7 = female pin header, 8 pins [form="♀ (female)"]
  J8 = female pin header, 8 pins [form="♀ (female)"]
  J9 = female pin header, 8 pins [form="♀ (female)"]
  J10 = female pin header, 8 pins [form="♀ (female)"]
  J11 = female pin header, 8 pins [form="♀ (female)"]
  J12 = female pin header, 8 pins [form="♀ (female)"]
  J16 = female pin header, 4 pins [form="♀ (female)"]
  J17 = female pin header, 4 pins [form="♀ (female)"]
  J18 = female pin header, 4 pins [form="♀ (female)"]
  MCP23017_5 = MCP23017 [chip_label="MCP23017\n" package="DIP (Dual Inline) [THT]"]
  J26 = female pin header, 8 pins [form="♀ (female)"]
  J27 = female pin header, 8 pins [form="♀ (female)"]
  J28 = female pin header, 8 pins [form="♀ (female)"]
  J29 = female pin header, 8 pins [form="♀ (female)"]
  J30 = female pin header, 8 pins [form="♀ (female)"]
  J31 = female pin header, 8 pins [form="♀ (female)"]
  J32 = female pin header, 8 pins [form="♀ (female)"]
  J33 = female pin header, 8 pins [form="♀ (female)"]
  J34 = female pin header, 8 pins [form="♀ (female)"]
  J35 = female pin header, 8 pins [form="♀ (female)"]
  J36 = female pin header, 4 pins [form="♀ (female)"]
  J37 = female pin header, 4 pins [form="♀ (female)"]
  J38 = female pin header, 4 pins [form="♀ (female)"]
  J39 = female pin header, 4 pins [form="♀ (female)"]
  J40 = female pin header, 4 pins [form="♀ (female)"]
  J41 = female pin header, 4 pins [form="♀ (female)"]
  J42 = female pin header, 4 pins [form="♀ (female)"]
  J43 = female pin header, 4 pins [form="♀ (female)"]
  J44 = female pin header, 4 pins [form="♀ (female)"]
  J45 = female pin header, 4 pins [form="♀ (female)"]
  J46 = female pin header, 4 pins [form="♀ (female)"]
  J47 = female pin header, 4 pins [form="♀ (female)"]
  J48 = female pin header, 4 pins [form="♀ (female)"]
  J49 = female pin header, 4 pins [form="♀ (female)"]
  J50 = female pin header, 4 pins [form="♀ (female)"]
  J2 = female pin header, 4 pins [form="♀ (female)"]
  J54 = female pin header, 4 pins [form="♀ (female)"]
  J14 = female pin header, 4 pins [form="♀ (female)"]
  J13 = female pin header, 4 pins [form="♀ (female)"]

nets:
  N1: 74TH/HCT1.Y4, J42.pin4
  N2: 74TH/HCT1.Y6, J42.pin3
  N3: 74TH/HCT1.Z, J54.pin4
  N4: 74TH/HCT1.Y7, J42.pin2
  N5: 74TH/HCT1.Y5, J42.pin1
  VSS: 74TH/HCT1.E, 74TH/HCT1.Vee, 74TH/HCT1.GND, 74TH/HCT2.E, 74TH/HCT2.Vee, 74TH/HCT2.GND, 74TH/HCT3.E, 74TH/HCT3.Vee, 74TH/HCT3.GND, MCP23017_1.Vss, MCP23017_1.A0, MCP23017_1.A1, MCP23017_1.A2, MCP23017_2.Vss, MCP23017_2.A1, MCP23017_2.A2, MCP23017_3.Vss, MCP23017_3.A0, MCP23017_3.A2, MCP23017_4.Vss, MCP23017_4.A2, MCP23017_5.Vss, MCP23017_5.A0, MCP23017_5.A1, J26.pin1, J26.pin2, J26.pin3, J26.pin4, J26.pin5, J26.pin6, J26.pin7, J26.pin8, J27.pin1, J27.pin2, J27.pin3, J27.pin4, J27.pin5, J27.pin6, J27.pin7, J27.pin8, J28.pin1, J28.pin2, J28.pin3, J28.pin4, J28.pin5, J28.pin6, J28.pin7, J28.pin8, J29.pin1, J29.pin2, J29.pin3, J29.pin4, J29.pin5, J29.pin6, J29.pin7, J29.pin8, J30.pin1, J30.pin2, J30.pin3, J30.pin4, J30.pin5, J30.pin6, J30.pin7, J30.pin8, J31.pin1, J31.pin2, J31.pin3, J31.pin4, J31.pin5, J31.pin6, J31.pin7, J31.pin8, J32.pin1, J32.pin2, J32.pin3, J32.pin4, J32.pin5, J32.pin6, J32.pin7, J32.pin8, J33.pin1, J33.pin2, J33.pin3, J33.pin4, J33.pin5, J33.pin6, J33.pin7, J33.pin8, J34.pin1, J34.pin2, J34.pin3, J34.pin4, J34.pin5, J34.pin6, J34.pin7, J34.pin8, J35.pin1, J35.pin2, J35.pin3, J35.pin4, J35.pin5, J35.pin6, J35.pin7, J35.pin8, J36.pin1, J36.pin2, J36.pin3, J36.pin4, J39.pin1, J39.pin2, J39.pin3, J39.pin4, J41.pin1, J41.pin2, J41.pin3, J41.pin4, J43.pin1, J43.pin2, J43.pin3, J43.pin4, J46.pin1, J46.pin2, J46.pin3, J46.pin4, J49.pin1, J49.pin2, J49.pin3, J49.pin4, J14.pin1
  N6: 74TH/HCT1.S2, 74TH/HCT2.S2, 74TH/HCT3.S2, J2.pin3
  N7: 74TH/HCT1.S1, 74TH/HCT2.S1, 74TH/HCT3.S1, J2.pin2
  N8: 74TH/HCT1.S0, 74TH/HCT2.S0, 74TH/HCT3.S0, J2.pin1
  N9: 74TH/HCT1.Y3, J16.pin1
  N10: 74TH/HCT1.Y0, J16.pin2
  N11: 74TH/HCT1.Y1, J16.pin3
  N12: 74TH/HCT1.Y2, J16.pin4
  VDD: 74TH/HCT1.Vcc, 74TH/HCT2.Vcc, 74TH/HCT3.Vcc, MCP23017_1.Vdd, MCP23017_1.RESET, MCP23017_2.Vdd, MCP23017_2.A0, MCP23017_2.RESET, MCP23017_3.Vdd, MCP23017_3.A1, MCP23017_3.RESET, MCP23017_4.Vdd, MCP23017_4.A0, MCP23017_4.A1, MCP23017_4.RESET, MCP23017_5.Vdd, MCP23017_5.A2, MCP23017_5.RESET, J37.pin1, J37.pin2, J37.pin3, J37.pin4, J38.pin1, J38.pin2, J38.pin3, J38.pin4, J40.pin1, J40.pin2, J40.pin3, J40.pin4, J44.pin1, J44.pin2, J44.pin3, J44.pin4, J47.pin1, J47.pin2, J47.pin3, J47.pin4, J50.pin1, J50.pin2, J50.pin3, J50.pin4, J14.pin2
  N13: 74TH/HCT2.Y4, J45.pin4
  N14: 74TH/HCT2.Y6, J45.pin3
  N15: 74TH/HCT2.Z, J54.pin3
  N16: 74TH/HCT2.Y7, J45.pin2
  N17: 74TH/HCT2.Y5, J45.pin1
  N18: 74TH/HCT2.Y3, J17.pin1
  N19: 74TH/HCT2.Y0, J17.pin2
  N20: 74TH/HCT2.Y1, J17.pin3
  N21: 74TH/HCT2.Y2, J17.pin4
  N22: 74TH/HCT3.Y4, J48.pin4
  N23: 74TH/HCT3.Y6, J48.pin3
  N24: 74TH/HCT3.Z, J54.pin2
  N25: 74TH/HCT3.Y7, J48.pin2
  N26: 74TH/HCT3.Y5, J48.pin1
  N27: 74TH/HCT3.Y3, J18.pin1
  N28: 74TH/HCT3.Y0, J18.pin2
  N29: 74TH/HCT3.Y1, J18.pin3
  N30: 74TH/HCT3.Y2, J18.pin4
  N31: MCP23017_1.GPB0, J3.pin1
  N32: MCP23017_1.GPB1, J3.pin2
  N33: MCP23017_1.GPB2, J3.pin3
  N34: MCP23017_1.GBP3, J3.pin4
  N35: MCP23017_1.GBP4, J3.pin5
  N36: MCP23017_1.GPB5, J3.pin6
  N37: MCP23017_1.GPB6, J3.pin7
  N38: MCP23017_1.GPB7, J3.pin8
  N39: MCP23017_1.SCL, MCP23017_2.SCL, MCP23017_3.SCL, MCP23017_4.SCL, MCP23017_5.SCL, J13.pin4
  N40: MCP23017_1.SDA, MCP23017_2.SDA, MCP23017_3.SDA, MCP23017_4.SDA, MCP23017_5.SDA, J13.pin3
  N41: MCP23017_1.GPA0, J6.pin8
  N42: MCP23017_1.GPA1, J6.pin7
  N43: MCP23017_1.GPA2, J6.pin6
  N44: MCP23017_1.GPA3, J6.pin5
  N45: MCP23017_1.GPA4, J6.pin4
  N46: MCP23017_1.GPA5, J6.pin3
  N47: MCP23017_1.GPA6, J6.pin2
  N48: MCP23017_1.GPA7, J6.pin1
  N49: MCP23017_2.GPB0, J4.pin1
  N50: MCP23017_2.GPB1, J4.pin2
  N51: MCP23017_2.GPB2, J4.pin3
  N52: MCP23017_2.GBP3, J4.pin4
  N53: MCP23017_2.GBP4, J4.pin5
  N54: MCP23017_2.GPB5, J4.pin6
  N55: MCP23017_2.GPB6, J4.pin7
  N56: MCP23017_2.GPB7, J4.pin8
  N57: MCP23017_2.GPA0, J5.pin8
  N58: MCP23017_2.GPA1, J5.pin7
  N59: MCP23017_2.GPA2, J5.pin6
  N60: MCP23017_2.GPA3, J5.pin5
  N61: MCP23017_2.GPA4, J5.pin4
  N62: MCP23017_2.GPA5, J5.pin3
  N63: MCP23017_2.GPA6, J5.pin2
  N64: MCP23017_2.GPA7, J5.pin1
  N65: MCP23017_3.GPB0, J8.pin1
  N66: MCP23017_3.GPB1, J8.pin2
  N67: MCP23017_3.GPB2, J8.pin3
  N68: MCP23017_3.GBP3, J8.pin4
  N69: MCP23017_3.GBP4, J8.pin5
  N70: MCP23017_3.GPB5, J8.pin6
  N71: MCP23017_3.GPB6, J8.pin7
  N72: MCP23017_3.GPB7, J8.pin8
  N73: MCP23017_3.GPA0, J7.pin8
  N74: MCP23017_3.GPA1, J7.pin7
  N75: MCP23017_3.GPA2, J7.pin6
  N76: MCP23017_3.GPA3, J7.pin5
  N77: MCP23017_3.GPA4, J7.pin4
  N78: MCP23017_3.GPA5, J7.pin3
  N79: MCP23017_3.GPA6, J7.pin2
  N80: MCP23017_3.GPA7, J7.pin1
  N81: MCP23017_4.GPB0, J10.pin1
  N82: MCP23017_4.GPB1, J10.pin2
  N83: MCP23017_4.GPB2, J10.pin3
  N84: MCP23017_4.GBP3, J10.pin4
  N85: MCP23017_4.GBP4, J10.pin5
  N86: MCP23017_4.GPB5, J10.pin6
  N87: MCP23017_4.GPB6, J10.pin7
  N88: MCP23017_4.GPB7, J10.pin8
  N89: MCP23017_4.GPA0, J9.pin8
  N90: MCP23017_4.GPA1, J9.pin7
  N91: MCP23017_4.GPA2, J9.pin6
  N92: MCP23017_4.GPA3, J9.pin5
  N93: MCP23017_4.GPA4, J9.pin4
  N94: MCP23017_4.GPA5, J9.pin3
  N95: MCP23017_4.GPA6, J9.pin2
  N96: MCP23017_4.GPA7, J9.pin1
  N97: J11.pin1, MCP23017_5.GPA7
  N98: J11.pin2, MCP23017_5.GPA6
  N99: J11.pin3, MCP23017_5.GPA5
  N100: J11.pin4, MCP23017_5.GPA4
  N101: J11.pin5, MCP23017_5.GPA3
  N102: J11.pin6, MCP23017_5.GPA2
  N103: J11.pin7, MCP23017_5.GPA1
  N104: J11.pin8, MCP23017_5.GPA0
  N105: J12.pin1, MCP23017_5.GPB0
  N106: J12.pin2, MCP23017_5.GPB1
  N107: J12.pin3, MCP23017_5.GPB2
  N108: J12.pin4, MCP23017_5.GBP3
  N109: J12.pin5, MCP23017_5.GBP4
  N110: J12.pin6, MCP23017_5.GPB5
  N111: J12.pin7, MCP23017_5.GPB6
  N112: J12.pin8, MCP23017_5.GPB7

notes:
  5v
  GND
  s2
  s1
  s0
  sda
  scl
  A2
  A1
  A0

custom parts:
  74TH/HCT4051: 8-channel analog multiplexer/demultiplexer
  MCP23017: 16-Bit I/O expander with serial interface
