# Fritzing sketch bombatuino (saved by Fritzing 0.7.11b)
breadboards: 8
stripboards: 1

parts:
  DIN1 = DIN-5 jack (MIDI) [package=THT]
  R1 = Resistor [tolerance=±5% resistance=220 package=THT]
  Arduino2 = Arduino
  R8 = Rotary Potentiometer (Small) [maximum_resistance=100kΩ]
  R9 = Rotary Potentiometer (Small) [maximum_resistance=100kΩ]
  R10 = Rotary Potentiometer (Small) [maximum_resistance=100kΩ]
  R11 = Rotary Potentiometer (Small) [maximum_resistance=100kΩ]
  R14 = Rotary Potentiometer (Small) [maximum_resistance=100kΩ]
  R15 = Rotary Potentiometer (Small) [maximum_resistance=100kΩ]
  74TH/HCT6 = 74TH/HCT4051 [chip_label="74TH 4051" package="DIP (Dual Inline) [THT]"]
  R16 = Rotary Potentiometer (Small) [maximum_resistance=100kΩ]
  R17 = Rotary Potentiometer (Small) [maximum_resistance=100kΩ]
  R18 = Rotary Potentiometer (Small) [maximum_resistance=100kΩ]
  R19 = Rotary Potentiometer (Small) [maximum_resistance=100kΩ]
  R13 = Rotary Potentiometer (Small) [maximum_resistance=100kΩ]
  R12 = Rotary Potentiometer (Small) [maximum_resistance=100kΩ]
  R20 = Rotary Potentiometer (Small) [maximum_resistance=100kΩ]
  R21 = Rotary Potentiometer (Small) [maximum_resistance=100kΩ]
  RE1 = Rotary Encoder [package=THT]
  74TH/HCT7 = 74TH/HCT4051 [chip_label="74TH 4051" package="DIP (Dual Inline) [THT]"]
  R22 = Slide Potentiometer [maximum_resistance=100kΩ]
  R25 = Slide Potentiometer [maximum_resistance=100kΩ]
  R26 = Slide Potentiometer [maximum_resistance=100kΩ]
  R27 = Slide Potentiometer [maximum_resistance=100kΩ]
  R28 = Slide Potentiometer [maximum_resistance=100kΩ]
  R29 = Slide Potentiometer [maximum_resistance=100kΩ]
  74TH/HCT8 = 74TH/HCT4051 [chip_label="74TH 4051" package="DIP (Dual Inline) [THT]"]
  RE2 = Rotary Encoder [package=THT]
  RE3 = Rotary Encoder [package=THT]
  74TH/HCT9 = 74TH/HCT4051 [chip_label="74TH 4051" package="DIP (Dual Inline) [THT]"]
  S1 = Pushbutton [package="[THT]"]
  R30 = Resistor [tolerance=±5% resistance=220 package=THT]
  S2 = Pushbutton [package="[THT]"]
  R31 = Resistor [tolerance=±5% resistance=220 package=THT]
  S3 = Pushbutton [package="[THT]"]
  R32 = Resistor [tolerance=±5% resistance=220 package=THT]
  S4 = Pushbutton [package="[THT]"]
  R33 = Resistor [tolerance=±5% resistance=220 package=THT]
  S5 = Pushbutton [package="[THT]"]
  S6 = Pushbutton [package="[THT]"]
  S7 = Pushbutton [package="[THT]"]
  S8 = Pushbutton [package="[THT]"]
  S9 = Pushbutton [package="[THT]"]
  S10 = Pushbutton [package="[THT]"]
  S11 = Pushbutton [package="[THT]"]
  S12 = Pushbutton [package="[THT]"]
  S13 = Pushbutton [package="[THT]"]
  S14 = Pushbutton [package="[THT]"]
  S15 = Pushbutton [package="[THT]"]
  S16 = Pushbutton [package="[THT]"]
  R34 = Resistor [tolerance=±5% resistance=220 package=THT]
  R35 = Resistor [tolerance=±5% resistance=220 package=THT]
  R36 = Resistor [tolerance=±5% resistance=220 package=THT]
  R37 = Resistor [tolerance=±5% resistance=220 package=THT]
  R38 = Resistor [tolerance=±5% resistance=220 package=THT]
  R39 = Resistor [tolerance=±5% resistance=220 package=THT]
  R40 = Resistor [tolerance=±5% resistance=220 package=THT]
  R41 = Resistor [tolerance=±5% resistance=220 package=THT]
  R42 = Resistor [tolerance=±5% resistance=220 package=THT]
  R43 = Resistor [tolerance=±5% resistance=220 package=THT]
  R44 = Resistor [tolerance=±5% resistance=220 package=THT]
  R45 = Resistor [tolerance=±5% resistance=220 package=THT]
  MCP23017_1 = MCP23017 [chip_label="MCP23017\n" package="DIP (Dual Inline) [THT]"]
  S17 = Pushbutton [package="[THT]"]
  R46 = Resistor [tolerance=±5% resistance=220 package=THT]
  S18 = Pushbutton [package="[THT]"]
  R47 = Resistor [tolerance=±5% resistance=220 package=THT]
  S19 = Pushbutton [package="[THT]"]
  R48 = Resistor [tolerance=±5% resistance=220 package=THT]
  S20 = Pushbutton [package="[THT]"]
  R49 = Resistor [tolerance=±5% resistance=220 package=THT]
  S21 = Pushbutton [package="[THT]"]
  S22 = Pushbutton [package="[THT]"]
  S23 = Pushbutton [package="[THT]"]
  S24 = Pushbutton [package="[THT]"]
  S25 = Pushbutton [package="[THT]"]
  S26 = Pushbutton [package="[THT]"]
  S27 = Pushbutton [package="[THT]"]
  S28 = Pushbutton [package="[THT]"]
  S29 = Pushbutton [package="[THT]"]
  S30 = Pushbutton [package="[THT]"]
  S31 = Pushbutton [package="[THT]"]
  S32 = Pushbutton [package="[THT]"]
  R50 = Resistor [tolerance=±5% resistance=220 package=THT]
  R51 = Resistor [tolerance=±5% resistance=220 package=THT]
  R52 = Resistor [tolerance=±5% resistance=220 package=THT]
  R53 = Resistor [tolerance=±5% resistance=220 package=THT]
  R54 = Resistor [tolerance=±5% resistance=220 package=THT]
  R55 = Resistor [tolerance=±5% resistance=220 package=THT]
  R56 = Resistor [tolerance=±5% resistance=220 package=THT]
  R57 = Resistor [tolerance=±5% resistance=220 package=THT]
  R58 = Resistor [tolerance=±5% resistance=220 package=THT]
  R59 = Resistor [tolerance=±5% resistance=220 package=THT]
  R60 = Resistor [tolerance=±5% resistance=220 package=THT]
  R61 = Resistor [tolerance=±5% resistance=220 package=THT]
  MCP23017_2 = MCP23017 [chip_label="MCP23017\n" package="DIP (Dual Inline) [THT]"]
  S65 = Pushbutton [package="[THT]"]
  R94 = Resistor [tolerance=±5% resistance=220 package=THT]
  S66 = Pushbutton [package="[THT]"]
  R95 = Resistor [tolerance=±5% resistance=220 package=THT]
  S67 = Pushbutton [package="[THT]"]
  R96 = Resistor [tolerance=±5% resistance=220 package=THT]
  S68 = Pushbutton [package="[THT]"]
  R97 = Resistor [tolerance=±5% resistance=220 package=THT]
  S69 = Pushbutton [package="[THT]"]
  S70 = Pushbutton [package="[THT]"]
  S71 = Pushbutton [package="[THT]"]
  S72 = Pushbutton [package="[THT]"]
  S73 = Pushbutton [package="[THT]"]
  S74 = Pushbutton [package="[THT]"]
  S75 = Pushbutton [package="[THT]"]
  S76 = Pushbutton [package="[THT]"]
  S77 = Pushbutton [package="[THT]"]
  S78 = Pushbutton [package="[THT]"]
  S79 = Pushbutton [package="[THT]"]
  S80 = Pushbutton [package="[THT]"]
  R98 = Resistor [tolerance=±5% resistance=220 package=THT]
  R99 = Resistor [tolerance=±5% resistance=220 package=THT]
  R100 = Resistor [tolerance=±5% resistance=220 package=THT]
  R101 = Resistor [tolerance=±5% resistance=220 package=THT]
  R102 = Resistor [tolerance=±5% resistance=220 package=THT]
  R103 = Resistor [tolerance=±5% resistance=220 package=THT]
  R104 = Resistor [tolerance=±5% resistance=220 package=THT]
  R105 = Resistor [tolerance=±5% resistance=220 package=THT]
  R106 = Resistor [tolerance=±5% resistance=220 package=THT]
  R107 = Resistor [tolerance=±5% resistance=220 package=THT]
  R108 = Resistor [tolerance=±5% resistance=220 package=THT]
  R109 = Resistor [tolerance=±5% resistance=220 package=THT]
  MCP23017_5 = MCP23017 [chip_label="MCP23017\n" package="DIP (Dual Inline) [THT]"]

nets:
  N1: DIN1.5, Arduino2.D1TX
  GND: DIN1.2, Arduino2.GND, R8.leg2, R9.leg2, R10.leg2, R11.leg2, R14.leg2, R15.leg2, 74TH/HCT6.GND, R16.leg2, R18.leg2, R19.leg2, R13.leg2, R12.leg2, R20.leg2, R21.leg2, RE1.EncoderPinB, 74TH/HCT7.GND, R22.leg1, R25.leg1, R26.leg1, R27.leg1, R28.leg1, R29.leg1, 74TH/HCT8.GND, RE2.EncoderPinB, RE3.EncoderPinB, 74TH/HCT9.GND, R30.Pin_1, R31.Pin_1, R32.Pin_1, R33.Pin_1, R34.Pin_1, R35.Pin_1, R36.Pin_1, R37.Pin_1, R38.Pin_1, R39.Pin_1, R40.Pin_1, R41.Pin_1, R42.Pin_1, R43.Pin_1, R44.Pin_1, MCP23017_1.Vss, MCP23017_1.A0, MCP23017_1.A1, MCP23017_1.A2, R46.Pin_1, R47.Pin_1, R48.Pin_1, R49.Pin_1, R50.Pin_1, R51.Pin_1, R52.Pin_1, R53.Pin_1, R54.Pin_1, R55.Pin_1, R56.Pin_1, R57.Pin_1, R58.Pin_1, R59.Pin_1, R60.Pin_1, MCP23017_2.Vss, MCP23017_2.A0, MCP23017_2.A1, R94.Pin_1, R95.Pin_1, R96.Pin_1, R97.Pin_1, R98.Pin_1, R99.Pin_1, R100.Pin_1, R101.Pin_1, R102.Pin_1, R103.Pin_1, R104.Pin_1, R105.Pin_1, R106.Pin_1, R107.Pin_1, R108.Pin_1, MCP23017_5.Vss, MCP23017_5.A0, MCP23017_5.A2
  N2: DIN1.4, R1.Pin_0
  VCC: R1.Pin_1, Arduino2.+5V, R8.leg1, R9.leg1, R10.leg1, R11.leg1, R14.leg1, R15.leg1, 74TH/HCT6.Vcc, R16.leg1, R17.leg1, R17.leg2, R18.leg1, R19.leg1, R13.leg1, R12.leg1, R20.leg1, R21.leg1, RE1.EncoderPinA, 74TH/HCT7.Vcc, R22.leg2, R25.leg2, R26.leg2, R27.leg2, R28.leg2, R29.leg2, 74TH/HCT8.Vcc, RE2.EncoderPinA, RE3.EncoderPinA, 74TH/HCT9.Vcc, S1.Pin_3, S1.Pin_4, S2.Pin_3, S2.Pin_4, S3.Pin_3, S3.Pin_4, S4.Pin_3, S4.Pin_4, S5.Pin_3, S5.Pin_4, S6.Pin_3, S6.Pin_4, S7.Pin_3, S7.Pin_4, S8.Pin_3, S8.Pin_4, S9.Pin_3, S9.Pin_4, S10.Pin_3, S10.Pin_4, S11.Pin_3, S11.Pin_4, S12.Pin_3, S12.Pin_4, S13.Pin_3, S13.Pin_4, S14.Pin_3, S14.Pin_4, S15.Pin_3, S15.Pin_4, S16.Pin_3, S16.Pin_4, MCP23017_1.Vdd, S17.Pin_3, S17.Pin_4, S18.Pin_3, S18.Pin_4, S19.Pin_3, S19.Pin_4, S20.Pin_3, S20.Pin_4, S21.Pin_3, S21.Pin_4, S22.Pin_3, S22.Pin_4, S23.Pin_3, S23.Pin_4, S24.Pin_3, S24.Pin_4, S25.Pin_3, S25.Pin_4, S26.Pin_3, S26.Pin_4, S27.Pin_3, S27.Pin_4, S28.Pin_3, S28.Pin_4, S29.Pin_3, S29.Pin_4, S30.Pin_3, S30.Pin_4, S31.Pin_3, S31.Pin_4, S32.Pin_3, S32.Pin_4, MCP23017_2.Vdd, MCP23017_2.A2, S65.Pin_3, S65.Pin_4, S66.Pin_3, S66.Pin_4, S67.Pin_3, S67.Pin_4, S68.Pin_3, S68.Pin_4, S69.Pin_3, S69.Pin_4, S70.Pin_3, S70.Pin_4, S71.Pin_3, S71.Pin_4, S72.Pin_3, S72.Pin_4, S73.Pin_3, S73.Pin_4, S74.Pin_3, S74.Pin_4, S75.Pin_3, S75.Pin_4, S76.Pin_3, S76.Pin_4, S77.Pin_3, S77.Pin_4, S78.Pin_3, S78.Pin_4, S79.Pin_3, S79.Pin_4, S80.Pin_3, S80.Pin_4, MCP23017_5.Vdd, MCP23017_5.A1
  N3: Arduino2.D13, Arduino2.D12, 74TH/HCT6.S1, 74TH/HCT7.S1, 74TH/HCT8.S1
  N4: Arduino2.D11, 74TH/HCT6.S0, 74TH/HCT7.S0, 74TH/HCT8.S0
  N5: Arduino2.D10, 74TH/HCT9.S2
  N6: Arduino2.D9, 74TH/HCT9.S1
  N7: Arduino2.D8, 74TH/HCT9.S0
  N8: Arduino2.A0, 74TH/HCT9.Z
  N9: Arduino2.A4, MCP23017_1.SDA, MCP23017_2.SDA, MCP23017_5.SDA
  N10: Arduino2.A5, MCP23017_1.SCL, MCP23017_2.SCL, MCP23017_5.SCL
  N11: R8.wiper, 74TH/HCT6.Y5
  N12: R9.wiper, 74TH/HCT6.Y7
  N13: R10.wiper, 74TH/HCT6.Y3
  N14: R11.wiper, 74TH/HCT6.Y0
  N15: R14.wiper, 74TH/HCT6.Y6
  N16: R15.wiper, 74TH/HCT6.Y4
  N17: 74TH/HCT6.Z, 74TH/HCT9.Y4
  N18: 74TH/HCT6.S2, 74TH/HCT7.S2, 74TH/HCT8.S2
  N19: 74TH/HCT6.Y1, R12.wiper
  N20: 74TH/HCT6.Y2, R13.wiper
  N21: R16.wiper, 74TH/HCT7.Y5
  N22: R17.wiper, 74TH/HCT7.Y7
  N23: R18.wiper, 74TH/HCT7.Y6
  N24: R19.wiper, 74TH/HCT7.Y4
  N25: R20.wiper, 74TH/HCT7.Y2
  N26: R21.wiper, 74TH/HCT7.Y1
  N27: RE1.EncoderPinC, 74TH/HCT7.Y0
  N28: 74TH/HCT7.Z, 74TH/HCT9.Y6
  N29: R22.wiper, 74TH/HCT8.Y4
  N30: R25.wiper, 74TH/HCT8.Y7
  N31: R26.wiper, 74TH/HCT8.Y6
  N32: R27.wiper, 74TH/HCT8.Y1
  N33: R28.wiper, 74TH/HCT8.Y2
  N34: R29.wiper, 74TH/HCT8.Y0
  N35: 74TH/HCT8.Z, 74TH/HCT9.Y7
  N36: 74TH/HCT8.Y5, RE3.EncoderPinC
  N37: 74TH/HCT8.Y3, RE2.EncoderPinC
  N38: S1.Pin_1, S1.Pin_2, R30.Pin_0, MCP23017_1.GPA0
  N39: S2.Pin_1, S2.Pin_2, R31.Pin_0, MCP23017_1.GPB7
  N40: S3.Pin_1, S3.Pin_2, R32.Pin_0, MCP23017_1.GPA1
  N41: S4.Pin_1, S4.Pin_2, R33.Pin_0, MCP23017_1.GPB6
  N42: S5.Pin_1, S5.Pin_2, R34.Pin_0, MCP23017_1.GPA2
  N43: S6.Pin_1, S6.Pin_2, R40.Pin_0, MCP23017_1.GPB5
  N44: S7.Pin_1, S7.Pin_2, R35.Pin_0, MCP23017_1.GPA3
  N45: S8.Pin_1, S8.Pin_2, R41.Pin_0, MCP23017_1.GBP4
  N46: S9.Pin_1, S9.Pin_2, R36.Pin_0, MCP23017_1.GPA4
  N47: S10.Pin_1, S10.Pin_2, R42.Pin_0, MCP23017_1.GBP3
  N48: S11.Pin_1, S11.Pin_2, R37.Pin_0, MCP23017_1.GPA5
  N49: S12.Pin_1, S12.Pin_2, R43.Pin_0, MCP23017_1.GPB2
  N50: S13.Pin_1, S13.Pin_2, R38.Pin_0, MCP23017_1.GPA6
  N51: S14.Pin_1, S14.Pin_2, R44.Pin_0, MCP23017_1.GPB1
  N52: S15.Pin_1, S15.Pin_2, R39.Pin_0, MCP23017_1.GPA7
  N53: S16.Pin_1, S16.Pin_2, R45.Pin_1, MCP23017_1.GPB0
  N54: S17.Pin_1, S17.Pin_2, R46.Pin_0, MCP23017_2.GPA0
  N55: S18.Pin_1, S18.Pin_2, R47.Pin_0, MCP23017_2.GPB7
  N56: S19.Pin_1, S19.Pin_2, R48.Pin_0, MCP23017_2.GPA1
  N57: S20.Pin_1, S20.Pin_2, R49.Pin_0, MCP23017_2.GPB6
  N58: S21.Pin_1, S21.Pin_2, R50.Pin_0, MCP23017_2.GPA2
  N59: S22.Pin_1, S22.Pin_2, R56.Pin_0, MCP23017_2.GPB5
  N60: S23.Pin_1, S23.Pin_2, R51.Pin_0, MCP23017_2.GPA3
  N61: S24.Pin_1, S24.Pin_2, R57.Pin_0, MCP23017_2.GBP4
  N62: S25.Pin_1, S25.Pin_2, R52.Pin_0, MCP23017_2.GPA4
  N63: S26.Pin_1, S26.Pin_2, R58.Pin_0, MCP23017_2.GBP3
  N64: S27.Pin_1, S27.Pin_2, R53.Pin_0, MCP23017_2.GPA5
  N65: S28.Pin_1, S28.Pin_2, R59.Pin_0, MCP23017_2.GPB2
  N66: S29.Pin_1, S29.Pin_2, R54.Pin_0, MCP23017_2.GPA6
  N67: S30.Pin_1, S30.Pin_2, R60.Pin_0, MCP23017_2.GPB1
  N68: S31.Pin_1, S31.Pin_2, R55.Pin_0, MCP23017_2.GPA7
  N69: S32.Pin_1, S32.Pin_2, R61.Pin_1, MCP23017_2.GPB0
  N70: S65.Pin_1, S65.Pin_2, R94.Pin_0, MCP23017_5.GPA0
  N71: S66.Pin_1, S66.Pin_2, R95.Pin_0, MCP23017_5.GPB7
  N72: S67.Pin_1, S67.Pin_2, R96.Pin_0, MCP23017_5.GPA1
  N73: S68.Pin_1, S68.Pin_2, R97.Pin_0, MCP23017_5.GPB6
  N74: S69.Pin_1, S69.Pin_2, R98.Pin_0, MCP23017_5.GPA2
  N75: S70.Pin_1, S70.Pin_2, R104.Pin_0, MCP23017_5.GPB5
  N76: S71.Pin_1, S71.Pin_2, R99.Pin_0, MCP23017_5.GPA3
  N77: S72.Pin_1, S72.Pin_2, R105.Pin_0, MCP23017_5.GBP4
  N78: S73.Pin_1, S73.Pin_2, R100.Pin_0, MCP23017_5.GPA4
  N79: S74.Pin_1, S74.Pin_2, R106.Pin_0, MCP23017_5.GBP3
  N80: S75.Pin_1, S75.Pin_2, R101.Pin_0, MCP23017_5.GPA5
  N81: S76.Pin_1, S76.Pin_2, R107.Pin_0, MCP23017_5.GPB2
  N82: S77.Pin_1, S77.Pin_2, R102.Pin_0, MCP23017_5.GPA6
  N83: S78.Pin_1, S78.Pin_2, R108.Pin_0, MCP23017_5.GPB1
  N84: S79.Pin_1, S79.Pin_2, R103.Pin_0, MCP23017_5.GPA7
  N85: S80.Pin_1, S80.Pin_2, R109.Pin_1, MCP23017_5.GPB0

custom parts:
  74TH/HCT4051: 8-channel analog multiplexer/demultiplexer
  MCP23017: 16-Bit I/O expander with serial interface
