# Fritzing sketch input_Platte (saved by Fritzing 0.7.11b)
stripboards: 2

parts:
  MCP23017_1 = MCP23017 [chip_label="MCP23017\n" package="DIP (Dual Inline) [THT]"]
  MCP23017_2 = MCP23017 [chip_label="MCP23017\n" package="DIP (Dual Inline) [THT]"]
  MCP23017_3 = MCP23017 [chip_label="MCP23017\n" package="DIP (Dual Inline) [THT]"]
  74TH/HCT1 = 74TH/HCT4051 [chip_label="74TH 4051" package="DIP (Dual Inline) [THT]"]
  74TH/HCT2 = 74TH/HCT4051 [chip_label="74TH 4051" package="DIP (Dual Inline) [THT]"]
  74TH/HCT3 = 74TH/HCT4051 [chip_label="74TH 4051" package="DIP (Dual Inline) [THT]"]
  J1 = female pin header, 8 pins [form="♀ (female)"]
  J2 = female pin header, 8 pins [form="♀ (female)"]
  J3 = female pin header, 8 pins [form="♀ (female)"]
  J4 = female pin header, 8 pins [form="♀ (female)"]
  J5 = female pin header, 8 pins [form="♀ (female)"]
  J6 = female pin header, 4 pins [form="♀ (female)"]
  J7 = female pin header, 4 pins [form="♀ (female)"]
  J8 = female pin header, 4 pins [form="♀ (female)"]
  J9 = female pin header, 5 pins [form="♀ (female)"]
  J10 = female pin header, 5 pins [form="♀ (female)"]
  J11 = female pin header, 3 pins [form="♀ (female)"]
  J12 = female pin header, 2 pins [form="♀ (female)"]
  J13 = female pin header, 2 pins [form="♀ (female)"]
  J14 = female pin header, 8 pins [form="♀ (female)"]
  J15 = female pin header, 5 pins [form="♀ (female)"]

nets:
  N1: MCP23017_1.GPB0, J1.pin1
  N2: MCP23017_1.GPB1, J1.pin2
  N3: MCP23017_1.GPB2, J1.pin3
  N4: MCP23017_1.GBP3, J1.pin4
  N5: MCP23017_1.GBP4, J1.pin5
  N6: MCP23017_1.GPB5, J1.pin6
  N7: MCP23017_1.GPB6, J1.pin7
  N8: MCP23017_1.GPB7, J1.pin8
  VSS: MCP23017_1.Vss, 74TH/HCT3.E, 74TH/HCT3.Vee, 74TH/HCT3.GND, J13.pin1
  N9: MCP23017_1.SCL, MCP23017_3.SCL
  N10: MCP23017_1.A0, MCP23017_1.A1, MCP23017_1.A2
  N11: MCP23017_1.GPA0, J2.pin8
  N12: MCP23017_1.GPA1, J2.pin7
  N13: MCP23017_1.GPA2, J2.pin6
  N14: MCP23017_1.GPA3, J2.pin5
  N15: MCP23017_1.GPA4, J2.pin4
  N16: MCP23017_1.GPA5, J2.pin3
  N17: MCP23017_1.GPA6, J2.pin2
  N18: MCP23017_1.GPA7, J2.pin1
  N19: MCP23017_2.GPB0, J3.pin1
  N20: MCP23017_2.GPB1, J3.pin2
  N21: MCP23017_2.GPB2, J3.pin3
  N22: MCP23017_2.GBP3, J3.pin4
  N23: MCP23017_2.GBP4, J3.pin5
  N24: MCP23017_2.GPB5, J3.pin6
  N25: MCP23017_2.GPB6, J3.pin7
  N26: MCP23017_2.GPB7, J3.pin8
  N27: MCP23017_2.SCL, J12.pin1
  N28: MCP23017_2.SDA, MCP23017_3.SDA, J12.pin2
  N29: MCP23017_2.A1, MCP23017_2.A2
  N30: MCP23017_2.GPA0, J4.pin8
  N31: MCP23017_2.GPA1, J4.pin7
  N32: MCP23017_2.GPA2, J4.pin6
  N33: MCP23017_2.GPA3, J4.pin5
  N34: MCP23017_2.GPA4, J4.pin4
  N35: MCP23017_2.GPA5, J4.pin3
  N36: MCP23017_2.GPA6, J4.pin2
  N37: MCP23017_2.GPA7, J4.pin1
  N38: MCP23017_3.GPB0, J5.pin1
  N39: MCP23017_3.GPB1, J5.pin2
  N40: MCP23017_3.GPB2, J5.pin3
  N41: MCP23017_3.GBP3, J5.pin4
  N42: MCP23017_3.GBP4, J5.pin5
  N43: MCP23017_3.GPB5, J5.pin6
  N44: MCP23017_3.GPB6, J5.pin7
  N45: MCP23017_3.GPB7, J5.pin8
  VCC: MCP23017_3.Vdd, MCP23017_3.RESET, 74TH/HCT1.Vcc, 74TH/HCT2.Vcc, 74TH/HCT3.Vcc, J13.pin2
  N46: MCP23017_3.GPA0, J14.pin8
  N47: MCP23017_3.GPA1, J14.pin7
  N48: MCP23017_3.GPA2, J14.pin6
  N49: MCP23017_3.GPA3, J14.pin5
  N50: MCP23017_3.GPA4, J14.pin4
  N51: MCP23017_3.GPA5, J14.pin3
  N52: MCP23017_3.GPA6, J14.pin2
  N53: MCP23017_3.GPA7, J14.pin1
  N54: 74TH/HCT1.Y4, J10.pin5
  N55: 74TH/HCT1.Y6, J10.pin4
  N56: 74TH/HCT1.Z, J10.pin3
  N57: 74TH/HCT1.Y7, J10.pin2
  N58: 74TH/HCT1.Y5, J10.pin1
  N59: 74TH/HCT1.E, 74TH/HCT1.Vee, 74TH/HCT1.GND
  N60: 74TH/HCT1.S2, 74TH/HCT2.S2, 74TH/HCT3.S0, J11.pin3
  N61: 74TH/HCT1.S1, 74TH/HCT2.S1, 74TH/HCT3.S1, J11.pin2
  N62: 74TH/HCT1.S0, 74TH/HCT2.S0, 74TH/HCT3.S2, J11.pin1
  N63: 74TH/HCT1.Y3, J6.pin1
  N64: 74TH/HCT1.Y0, J6.pin2
  N65: 74TH/HCT1.Y1, J6.pin3
  N66: 74TH/HCT1.Y2, J6.pin4
  N67: 74TH/HCT2.Y4, J9.pin5
  N68: 74TH/HCT2.Y6, J9.pin4
  N69: 74TH/HCT2.Z, J9.pin3
  N70: 74TH/HCT2.Y7, J9.pin2
  N71: 74TH/HCT2.Y5, J9.pin1
  N72: 74TH/HCT2.Vee, 74TH/HCT2.GND
  N73: 74TH/HCT2.Y3, J7.pin1
  N74: 74TH/HCT2.Y0, J7.pin2
  N75: 74TH/HCT2.Y1, J7.pin3
  N76: 74TH/HCT2.Y2, J7.pin4
  N77: 74TH/HCT3.Y4, J15.pin5
  N78: 74TH/HCT3.Y6, J15.pin4
  N79: 74TH/HCT3.Z, J15.pin3
  N80: 74TH/HCT3.Y7, J15.pin2
  N81: 74TH/HCT3.Y5, J15.pin1
  N82: 74TH/HCT3.Y3, J8.pin1
  N83: 74TH/HCT3.Y0, J8.pin2
  N84: 74TH/HCT3.Y1, J8.pin3
  N85: 74TH/HCT3.Y2, J8.pin4

custom parts:
  MCP23017: 16-Bit I/O expander with serial interface
  74TH/HCT4051: 8-channel analog multiplexer/demultiplexer
